# Fritzing sketch mutebox (saved by Fritzing 0.9.0b)
circuit board: 8.46667cm x 5.64444cm
breadboards: 1

parts:
  TRINKET1 = Trinket 3V
  IC1 = MCP23017 I2C I/O Expander
  BUTTON1 = Arcade Button (white)
  BUTTON2 = Arcade Button (white)
  ENCODER1 = Rotary Encoder with Knob
  R1 = Resistor [tolerance=±5% resistance=4.7k package=THT]
  R2 = Resistor [tolerance=±5% resistance=4.7k package=THT]

nets:
  N1: TRINKET1.no_name_yet#2, IC1.VSS, IC1.A0, IC1.A1, IC1.A2, BUTTON1.no_name_yet#2, BUTTON2.no_name_yet#2, ENCODER1.no_name_yet#2, ENCODER1.no_name_yet#5
  N2: TRINKET1.no_name_yet#7, IC1.SCL, R1.Pin_0
  N3: TRINKET1.no_name_yet#9, IC1.SDA, R2.Pin_0
  N4: TRINKET1.no_name_yet#10, IC1.VDD, IC1.INTB, R1.Pin_1, R2.Pin_1
  N5: IC1.GPB0, BUTTON2.no_name_yet#1
  N6: IC1.GPB1, BUTTON1.no_name_yet#1
  N7: IC1.GPA5, ENCODER1.no_name_yet#4
  N8: IC1.GPA6, ENCODER1.no_name_yet#3
  N9: IC1.GPA7, ENCODER1.no_name_yet#1

custom parts:
  Trinket 3V: Adafruit Trinket 3V
  MCP23017 I2C I/O Expander: MCP23017 I2C 16-Channel I/O Expander
  Arcade Button (white): Adafruit Arcade Button (white)
  Rotary Encoder with Knob: Rotary Encoder with 1/4" Shaft and Knob
